// Logisim project Projeto_SFI_main.circ as structural Verilog: 1 circuit, main circuit main
module main (
  input  in_1
);

  wire and_1_out, and_2_out, clock_1_out, comparator_1_eq, comparator_2_eq, comparator_4_lt, comparator_5_eq,
       decoder_1_out0, decoder_1_out1, decoder_1_out3, decoder_1_out4, decoder_1_out5, demultiplexer_1_out1,
       demultiplexer_1_out2, demultiplexer_1_out3, demultiplexer_1_out4, demultiplexer_1_out5,
       demultiplexer_1_out6, demultiplexer_1_out7, not_1_out, or_3_out, or_6_out, or_7_out, or_8_out;
  wire [0:0] or_1_out;
  wire [1:0] comparator_3_eq, decoder_1_out2, or_4_out;
  wire [2:0] multiplexer_3_out, multiplexer_5_out, multiplexer_6_out, multiplexer_7_out, rom_1_p3_2;
  wire [3:0] rom_1_p2_2;
  wire [3:1] rom_1_p2;
  wire [5:0] rom_1_p3;
  wire [7:0] adder_1_out, adder_2_out, adder_3_out, and_3_out, bit_extender_1_out, bit_extender_2_out,
       bit_extender_3_out, bit_extender_4_out, bit_extender_5_out, controlled_buffer_1_out,
       multiplexer_1_out, multiplexer_2_out, multiplexer_4_out, multiplexer_8_out, multiplexer_9_out,
       multiplexer_10_out, multiplexer_11_out, or_9_out, PC_q, R0_q, R1_q, R2_q, R3_q, R4_q, R5_q, R6_q,
       R7_q, ram_1_dout, shifter_1_out, subtractor_1_out;

  Clock clock_1 (.out(clock_1_out));
  Register PC (.D(multiplexer_1_out), .en(1'b1), .clk(clock_1_out), .Q(PC_q), .clr(in_1));
  Shifter shifter_1 (.in(multiplexer_8_out), .\dist (3'b001), .out(shifter_1_out));
  // ROM #(.line("dual")) rom_1: pin names not known; wires that end beside it: PC_q, {rom_1_p2_2, rom_1_p2, rom_1_p3_2[2]}, {rom_1_p3_2[1:0], rom_1_p3}
  not not_1 (not_1_out, comparator_5_eq);
  // Probe on adder_1_out
  Adder adder_1 (.a(PC_q), .b(shifter_1_out), .out(adder_1_out));  // open: cin, cout
  and and_1 (and_1_out, decoder_1_out4, comparator_5_eq);
  and and_2 (and_2_out, decoder_1_out5, not_1_out);
  Adder adder_2 (.a(8'h2), .b(PC_q), .out(adder_2_out));  // open: cin, cout
  or or_1 (or_1_out[0], and_1_out, and_2_out);
  Multiplexer #(.select(2), .width(8)) multiplexer_1 (
    .in0(adder_2_out), .in1(adder_1_out), .in2(adder_1_out), .out(multiplexer_1_out),
    .sel({decoder_1_out2[1], or_1_out[0]}));  // open: in3
  Demultiplexer #(.select(3)) demultiplexer_1 (
    .out1(demultiplexer_1_out1), .out2(demultiplexer_1_out2), .out3(demultiplexer_1_out3),
    .out4(demultiplexer_1_out4), .out5(demultiplexer_1_out5), .out6(demultiplexer_1_out6),
    .out7(demultiplexer_1_out7), .in(or_8_out), .sel(rom_1_p2));  // open: out0
  Comparator #(.width(4)) comparator_1 (.a(rom_1_p2_2), .b(4'b0100), .eq(comparator_1_eq));  // open: gt, lt
  Comparator #(.width(4)) comparator_2 (.a(rom_1_p2_2), .b(4'b0101), .eq(comparator_2_eq));  // open: gt, lt
  Register R0 (.D({8{1'b0}}), .clk(clock_1_out), .Q(R0_q), .clr(in_1));  // open: en
  Register R4 (.D(multiplexer_11_out), .en(demultiplexer_1_out4), .clk(clock_1_out), .Q(R4_q), .clr(in_1));
  Multiplexer #(.select(3), .width(8)) multiplexer_2 (
    .in0(R0_q), .in1(R1_q), .in2(R2_q), .in3(R3_q), .in4(R4_q), .in5(R5_q), .in6(R6_q), .in7(R7_q),
    .out(multiplexer_2_out), .sel(multiplexer_3_out));
  or or_2 (comparator_3_eq[1], comparator_1_eq, comparator_2_eq);
  Multiplexer #(.select(2), .width(3)) multiplexer_3 (
    .in0(rom_1_p3[5:3]), .in1(rom_1_p2), .in2(rom_1_p3_2), .out(multiplexer_3_out), .sel(comparator_3_eq));  // open: in3
  Comparator #(.width(4)) comparator_3 (.a(rom_1_p2_2), .b(4'b0011), .eq(comparator_3_eq[0]));  // open: gt, lt
  Register R1 (.D(multiplexer_11_out), .en(demultiplexer_1_out1), .clk(clock_1_out), .Q(R1_q), .clr(in_1));
  Register R5 (.D(multiplexer_11_out), .en(demultiplexer_1_out5), .clk(clock_1_out), .Q(R5_q), .clr(in_1));
  Multiplexer #(.select(3), .width(8)) multiplexer_4 (
    .in0(R0_q), .in1(R1_q), .in2(R2_q), .in3(R3_q), .in4(R4_q), .in5(R5_q), .in6(R6_q), .in7(R7_q),
    .out(multiplexer_4_out), .sel(multiplexer_5_out));
  Multiplexer #(.width(3)) multiplexer_5 (
    .in0(rom_1_p3_2), .in1(rom_1_p2), .out(multiplexer_5_out), .sel(comparator_3_eq[1]));
  Register R2 (.D(multiplexer_11_out), .en(demultiplexer_1_out2), .clk(clock_1_out), .Q(R2_q), .clr(in_1));
  Register R6 (.D(multiplexer_11_out), .en(demultiplexer_1_out6), .clk(clock_1_out), .Q(R6_q), .clr(in_1));
  Register R3 (.D(multiplexer_11_out), .en(demultiplexer_1_out3), .clk(clock_1_out), .Q(R3_q), .clr(in_1));
  Register R7 (.D(multiplexer_11_out), .en(demultiplexer_1_out7), .clk(clock_1_out), .Q(R7_q), .clr(in_1));
  or or_3 (or_3_out, decoder_1_out4, decoder_1_out5);
  or or_4 (or_4_out[0], decoder_1_out3, decoder_1_out2[1]);
  or or_5 (or_4_out[1], or_3_out, decoder_1_out2[1]);
  or or_6 (or_6_out, decoder_1_out1, decoder_1_out2[0]);
  Decoder #(.select(4)) decoder_1 (
    .out0(decoder_1_out0), .out1(decoder_1_out1), .out2(decoder_1_out2[0]), .out3(decoder_1_out3),
    .out4(decoder_1_out4), .out5(decoder_1_out5), .out6(decoder_1_out2[1]), .sel(rom_1_p2_2), .en(1'b1));  // open: out7, out8, out9, out10, out11, out12, out13, out14, out15
  or or_7 (or_7_out, decoder_1_out3, or_6_out);
  assign bit_extender_1_out = {{2{rom_1_p3[5]}}, rom_1_p3};  // Bit_Extender bit_extender_1
  assign bit_extender_2_out = {{2{1'b0}}, rom_1_p3};  // Bit_Extender bit_extender_2
  assign bit_extender_3_out = {{2{rom_1_p3[5]}}, rom_1_p3};  // Bit_Extender bit_extender_3
  Bit_Extender #(.in_width(9), .out_width(8)) bit_extender_4 (.in({rom_1_p3_2, rom_1_p3}), .out(bit_extender_4_out));
  // Probe on or_7_out
  Multiplexer #(.width(3)) multiplexer_6 (.in0(3'b000), .in1(3'b001), .out(multiplexer_6_out), .sel(or_3_out));
  Multiplexer #(.width(3)) multiplexer_7 (
    .in0(multiplexer_6_out), .in1(rom_1_p3[2:0]), .out(multiplexer_7_out), .sel(decoder_1_out0));
  Multiplexer #(.select(2), .width(8)) multiplexer_8 (
    .in0(bit_extender_1_out), .in1(bit_extender_2_out), .in2(bit_extender_3_out), .in3(bit_extender_4_out),
    .out(multiplexer_8_out), .sel(or_4_out));
  Multiplexer #(.width(8)) multiplexer_9 (
    .in0(multiplexer_2_out), .in1(multiplexer_8_out), .out(multiplexer_9_out), .sel(or_7_out));
  // Probe on multiplexer_7_out
  or or_8 (or_8_out, decoder_1_out0, or_6_out, decoder_1_out2[1]);
  Adder adder_3 (.a(multiplexer_4_out), .b(multiplexer_9_out), .out(adder_3_out));  // open: cin, cout
  Subtractor subtractor_1 (.a(multiplexer_4_out), .b(multiplexer_9_out), .out(subtractor_1_out));  // open: bin, bout
  assign or_9_out = multiplexer_4_out | multiplexer_9_out;  // OR_Gate or_9, 8 bits wide
  assign and_3_out = multiplexer_4_out & multiplexer_9_out;  // AND_Gate and_3, 8 bits wide
  Comparator comparator_4 (.a(multiplexer_4_out), .b(multiplexer_9_out), .lt(comparator_4_lt));  // open: gt, eq
  assign bit_extender_5_out = {{7{1'b0}}, comparator_4_lt};  // Bit_Extender bit_extender_5
  Multiplexer #(.select(3), .width(8)) multiplexer_10 (
    .in0(adder_3_out), .in1(subtractor_1_out), .in2(and_3_out), .in3(or_9_out), .in4(bit_extender_5_out),
    .in5({8{1'b0}}), .in6({8{1'b0}}), .in7({8{1'b0}}), .out(multiplexer_10_out), .sel(multiplexer_7_out));
  Comparator comparator_5 (.a({8{1'b0}}), .b(multiplexer_10_out), .eq(comparator_5_eq));  // open: gt, lt
  RAM #(.asyncread("true"), .trigger("falling")) ram_1 (
    .addr(multiplexer_10_out), .we(decoder_1_out3), .oe(decoder_1_out2[0]), .clk(clock_1_out),
    .din(multiplexer_2_out), .dout(ram_1_dout));
  assign controlled_buffer_1_out = decoder_1_out2[0] ? ram_1_dout : 8'bz;  // Controlled_Buffer controlled_buffer_1
  Multiplexer #(.select(2), .width(8)) multiplexer_11 (
    .in0(multiplexer_10_out), .in1(controlled_buffer_1_out), .in2(adder_2_out), .out(multiplexer_11_out),
    .sel(decoder_1_out2));  // open: in3

  // Notes on the sheet:
  //   contents of rom_1 (hex, n*v repeats v):
  //   22 10 24 11 26 12 28 13 a 5c 4a 9 b 14 4a 4 1c 2 1e 2 60 6 1c 1 1e 1 60 3 1c 0 1e 0 3c 20 3e 21 61
  //   ee
  //   imediato i
  //   imediato_s
  //   imediato_b
  //   imediato_J
  //   immsel
  //   Tipo I - 00
  //   Tipo s - 01
  //   Tipo b - 10
  //   Tipo j - 11
  //   instrucao tipo s
  //   instrucao tipo b
  //   alusrc
  //   instrucao tipo i
  //   instrucao tipo J
  //   aluop
  //   regwrite
endmodule
